# Fritzing sketch schematic (saved by Fritzing 1.0.0rc)
breadboards: 1

parts:
  Mod1 = Amica NodeMCU DEVKIT 1.0
  J1 = Basic Servo
  J2 = Basic Servo
  LED1 = smd LED [color="Red (633nm)" package="1206 [SMD]"]
  LED2 = smd LED [color="Red (633nm)" package="1206 [SMD]"]
  IC1 = ULN2003A [package="DIP16 [THT]"]
  J3 = Basic Servo
  LED3 = smd LED [color="Red (633nm)" package="1206 [SMD]"]

nets:
  N1: Mod1.pin1, Mod1.pin_10, Mod1.pin_26
  GND: Mod1.pin2, Mod1.pin_9, Mod1.pin_25, Mod1.pin_29, J1.gnd, J2.gnd, IC1.COM_-_Common, J3.gnd
  N2: Mod1.pin6, IC1.In_7
  N3: Mod1.pin7, IC1.In_4
  N4: Mod1.pin8, IC1.In_1
  N5: Mod1.pin_11, J3.pulse
  N6: Mod1.pin_13, J2.pulse
  N7: Mod1.pin_14, J1.pulse
  VCC: Mod1.pin_30, J1.vcc, J2.vcc, LED1.anode, LED2.anode, IC1.0V, J3.vcc, LED3.anode
  N8: LED1.cathode, IC1.Out_7
  N9: LED2.cathode, IC1.Out_4
  N10: IC1.Out_1, LED3.cathode

notes:
  You can power the entire board either through the MicroUSB port on the NodeMCU module or via the VCC and GND pins.
